// Digital circuit GPR.dig as structural Verilog
module GPR (
  input  CLK,
  input  [3:0] LOAD,
  input  [1:0] STORE,
  input  EN,
  output [3:0] GPR
);

  wire demultiplexer_1_out_0, demultiplexer_1_out_1, demultiplexer_1_out_2, demultiplexer_1_out_3;
  wire [3:0] R0_q, R1_q, R2_q, R3_q;

  Demultiplexer #(.Selector_Bits(2)) demultiplexer_1 (
    .sel(STORE), .in(EN), .out_0(demultiplexer_1_out_0), .out_1(demultiplexer_1_out_1),
    .out_2(demultiplexer_1_out_2), .out_3(demultiplexer_1_out_3));
  Register #(.Bits(4)) R0 (.D(LOAD), .C(CLK), .en(demultiplexer_1_out_0), .Q(R0_q));
  Register #(.Bits(4)) R1 (.D(LOAD), .C(CLK), .en(demultiplexer_1_out_1), .Q(R1_q));
  Register #(.Bits(4)) R2 (.D(LOAD), .C(CLK), .en(demultiplexer_1_out_2), .Q(R2_q));
  Register #(.Bits(4)) R3 (.D(LOAD), .C(CLK), .en(demultiplexer_1_out_3), .Q(R3_q));
  Multiplexer #(.Selector_Bits(2), .Bits(4)) multiplexer_1 (
    .sel(STORE), .in_0(R0_q), .in_1(R1_q), .in_2(R2_q), .in_3(R3_q), .out(GPR));
endmodule
