// Digital circuit IR.dig as structural Verilog
module IR (
  input  en,
  input  [1:0] s,
  input  C,
  input  [3:0] inst,
  output [3:0] IR
);

  Register #(.Bits(3)) u_IR (.D(inst[2:0]), .C(C), .en(en), .Q(IR[2:0]));
  Multiplexer #(.Selector_Bits(2)) multiplexer_1 (
    .sel(s), .in_0(IR[2]), .in_1(1'b0), .in_2(inst[0]), .in_3(inst[2]), .out(IR[3]));
endmodule
