// Digital circuit PC.dig as structural Verilog
module PC (
  input  [3:0] INC,
  input  C,
  input  abs,
  input  rel,
  input  RESET,
  output [3:0] Next,
  output [3:0] PC
);

  wire [3:0] Add_s, multiplexer_1_out, multiplexer_2_out;

  Register #(.Bits(4), .isProgramCounter("true")) u_PC (.D(multiplexer_2_out), .C(~C), .en(RESET), .Q(PC));
  Add #(.Bits(4)) Add_One (.a(PC), .b(4'b0001), .c_i(1'b0), .s(Next));  // open: c_o
  Add #(.Bits(4)) Add (.a(Next), .b(INC), .c_i(1'b0), .s(Add_s));  // open: c_o
  Multiplexer #(.Bits(4)) multiplexer_1 (.sel(rel), .in_0(Next), .in_1(Add_s), .out(multiplexer_1_out));
  Multiplexer #(.Bits(4)) multiplexer_2 (.sel(abs), .in_0(multiplexer_1_out), .in_1(INC), .out(multiplexer_2_out));

  // Notes on the sheet:
  //   PC: the current program counter
  //   {{de der aktuelle Programmzähler}}
  //   abs: Triggers a absolute jump.
  //   The value of the ALU input is used as the new address.
  //   {{de Absoluten Sprung auslösen. Der Wert des ALU 
  //   Eingangs wird als neue Adresse verwendet.}}
  //   rel: Triggers a relative jump. The value of the ALU 
  //   input is added to the current address.
  //   {{de relativen Spung auslösen. Der Wert des ALU 
  //   Eingangs wird zur aktuellen Adresse addiert.}}
endmodule
