// Digital circuit Registers_DRAM.dig as structural Verilog
module Registers_DRAM (
  input  RELATIVE_JUMP,
  input  ABSOLUTE_JUMP,
  input  RESET,
  input  clk,
  input  [3:0] INCREMENT,
  input  Input_source_select,
  input  CLK_2,
  input  EN,
  input  [1:0] s,
  input  CLK_3,
  input  EN_2,
  input  [1:0] store,
  input  CS,
  input  WE,
  input  OE,
  output [3:0] PC
);

  wire [3:0] gpr_1_gpr, ir_1_ir, multiplexer_1_out, ramsingleportsel_1_d;

  GPR gpr_1 (.CLK(CLK_3), .LOAD(ir_1_ir), .STORE(store), .EN(EN_2), .GPR(gpr_1_gpr));
  PC pc_1 (.INC(INCREMENT), .C(clk), .abs(RELATIVE_JUMP), .rel(ABSOLUTE_JUMP), .RESET(RESET), .Next(PC));  // open: PC
  Multiplexer #(.Bits(4)) multiplexer_1 (
    .sel(Input_source_select), .in_0(PC), .in_1(gpr_1_gpr), .out(multiplexer_1_out));
  RAMSinglePortSel #(.AddrBits(4), .isProgramMemory("true"), .Bits(4)) ramsingleportsel_1 (
    .A(multiplexer_1_out), .CS(CS), .WE(WE), .OE(OE), .D(ramsingleportsel_1_d));
  IR ir_1 (.en(EN), .s(s), .C(CLK_2), .inst(ramsingleportsel_1_d), .IR(ir_1_ir));
endmodule
